# Fritzing sketch Montage Final (saved by Fritzing 0.9.3b)
breadboards: 1

parts:
  Composant1 = Arduino Uno (Rev3)
  C1 = Ceramic Capacitor [capacitance=10nF package="100 mil [THT, multilayer]"]
  U1 = TOUCH [package=touch2]  # not connected
  D1 = Rectifier Diode [part_number=1N4001 package="300 mil [THT]"]
  R1 = Resistor [tolerance=±5% resistance=1M package=THT]
  C2 = Ceramic Capacitor [capacitance=0.1nF package="100 mil [THT, multilayer]"]
  L1 = Inductor [inductance=10mH package="400 mil [THT]"]
  R2 = Resistor [tolerance=±5% resistance=10k package=THT]
  R3 = Resistor [tolerance=±5% resistance=3.3k package=THT]
  R4 = Resistor [tolerance=±5% resistance=220 package=THT]
  R5 = Resistor [tolerance=±5% resistance=220 package=THT]
  R6 = Resistor [tolerance=±5% resistance=220 package=THT]
  LED1 = LED - 5mm [color="White (4500K)" package="5 mm [THT]"]
  LED2 = LED - 5mm [color="Red (633nm)" package="5 mm [THT]"]
  LED3 = LED - 5mm [color="Green (555nm)" package="5 mm [THT]"]

nets (from the breadboard view):
  N1: Composant1.A0, D1.cathode, R1.Pin_1, C2.0
  N2: Composant1.D9_PWM, R2.Pin_0
  N3: Composant1.GND, R3.Pin_1, LED1.cathode, LED2.cathode, LED3.cathode
  N4: Composant1.D2, R4.Pin_0, LED1.anode
  N5: Composant1.D3_PWM, R5.Pin_0, LED3.anode
  N6: Composant1.D4, R6.Pin_0
  N7: C1.0, D1.anode
  N8: C1.1, L1.pin_0
  N9: R1.Pin_0, C2.1
  N10: L1.pin_1, R2.Pin_1, R3.Pin_0
  N11: R6.Pin_1, LED2.anode

notes:
  Patate
